// Logisim project cpuv2.circ as structural Verilog: 4 circuits, main circuit main
module main (
);

  wire alu_1_jump0, clock_1_out, controlled_buffer_1_out, decoder_1_out0, decoder_1_out1, decoder_1_out4,
       decoder_1_out5, decoder_1_out12, decoder_1_out13, decoder_1_out14, decoder_1_out15, decoder_1_out16,
       decoder_1_out17, decoder_1_out18, decoder_1_out19, decoder_1_out20, decoder_1_out21, decoder_1_out22,
       decoder_1_out23, decoder_1_out24, decoder_1_out31, not_1_out, not_2_out, not_3_out, not_4_out,
       not_5_out, or_1_out, or_2_out, or_3_out, or_4_out, or_5_out;
  wire [4:0] bit_extender_1_out;
  wire [15:0] adder_1_out, adder_2_out, controlled_buffer_2_out, controlled_buffer_3_out, counter_1_q,
       multiplexer_1_out, multiplexer_2_out, multiplexer_3_out, multiplexer_4_out, multiplexer_5_out,
       multiplexer_6_out, multiplexer_7_out, multiplexer_8_out, multiplexer_9_out, ram_1_dout,
       registers_1_reg_out_0, registers_1_reg_out_1, rom_1_p2, rom_1_p3, rom_1_p4, rom_1_p5, stack_1_output_0;

  Clock clock_1 (.out(clock_1_out));
  assign controlled_buffer_1_out = not_1_out ? clock_1_out : 1'bz;  // Controlled_Buffer controlled_buffer_1
  not not_1 (not_1_out, decoder_1_out31);
  Adder #(.width(16)) adder_1 (.a(counter_1_q), .b(16'h4), .out(adder_1_out));  // open: cin, cout
  Counter #(.max('hffff), .width(16)) counter_1 (
    .clr(decoder_1_out15), .load(controlled_buffer_1_out), .clk(controlled_buffer_1_out),
    .D(multiplexer_1_out), .Q(counter_1_q));  // open: up, count, carry
  Multiplexer #(.width(16)) multiplexer_1 (
    .in0(adder_1_out), .in1(multiplexer_2_out), .out(multiplexer_1_out), .sel(or_2_out));
  // ROM #(.addrWidth(16), .dataWidth(16), .line("quad")) rom_1: pin names not known; wires that end beside it: counter_1_q, rom_1_p2, rom_1_p3, rom_1_p4, rom_1_p5
  Multiplexer #(.width(16)) multiplexer_2 (
    .in0(controlled_buffer_2_out), .in1(rom_1_p5), .out(multiplexer_2_out), .sel(not_2_out));
  not not_2 (not_2_out, decoder_1_out22);
  Multiplexer #(.width(16)) multiplexer_3 (
    .in0(rom_1_p4), .in1({16{1'b1}}), .out(multiplexer_3_out), .sel(decoder_1_out0));
  Multiplexer #(.width(16)) multiplexer_4 (
    .in0(rom_1_p3), .in1({16{1'b1}}), .out(multiplexer_4_out), .sel(decoder_1_out0));
  Multiplexer #(.width(16)) multiplexer_5 (.in0(rom_1_p5), .in1({16{1'b1}}), .out(multiplexer_5_out), .sel(or_1_out));
  or or_1 (or_1_out, decoder_1_out0, decoder_1_out16, decoder_1_out17, decoder_1_out24, decoder_1_out18, decoder_1_out19, decoder_1_out20);
  registers registers_1 (
    .reg_load_1(multiplexer_4_out), .reg_load_0(multiplexer_3_out), .clock(controlled_buffer_1_out),
    .reg_save(multiplexer_5_out), .reg_in(controlled_buffer_2_out), .reg_out_1(registers_1_reg_out_1),
    .reg_out_0(registers_1_reg_out_0));
  Bit_Extender #(.in_width(16), .out_width(5)) bit_extender_1 (.in(rom_1_p2), .out(bit_extender_1_out));
  Decoder #(.enable("false"), .select(5)) decoder_1 (
    .out0(decoder_1_out0), .out1(decoder_1_out1), .out4(decoder_1_out4), .out5(decoder_1_out5),
    .out12(decoder_1_out12), .out13(decoder_1_out13), .out14(decoder_1_out14), .out15(decoder_1_out15),
    .out16(decoder_1_out16), .out17(decoder_1_out17), .out18(decoder_1_out18), .out19(decoder_1_out19),
    .out20(decoder_1_out20), .out21(decoder_1_out21), .out22(decoder_1_out22), .out23(decoder_1_out23),
    .out24(decoder_1_out24), .out31(decoder_1_out31), .sel(bit_extender_1_out));  // open: out2, out3, out6, out7, out8, out9, out10, out11, out25, out26, out27, out28, out29, out30
  assign controlled_buffer_2_out = decoder_1_out1 ? rom_1_p3 : 16'bz;  // Controlled_Buffer controlled_buffer_2
  Multiplexer #(.width(16)) multiplexer_6 (
    .in0({16{1'b0}}), .in1(registers_1_reg_out_0), .out(multiplexer_6_out), .sel(decoder_1_out12));
  RAM #(.addrWidth(16), .dataWidth(16)) ram_1 (
    .addr(multiplexer_6_out), .we(decoder_1_out12), .oe(1'b1), .clk(controlled_buffer_1_out),
    .din(multiplexer_9_out), .dout(ram_1_dout));
  Adder #(.width(16)) adder_2 (.a(16'h4), .b(counter_1_q), .out(adder_2_out));  // open: cin, cout
  not not_3 (not_3_out, decoder_1_out4);
  or or_2 (or_2_out, alu_1_jump0, decoder_1_out21, decoder_1_out22);
  assign controlled_buffer_3_out = decoder_1_out21 ? adder_2_out : 16'bz;  // Controlled_Buffer controlled_buffer_3
  assign controlled_buffer_2_out = decoder_1_out23 ? ram_1_dout : 16'bz;  // Controlled_Buffer controlled_buffer_4
  Multiplexer #(.width(16)) multiplexer_7 (
    .in0(rom_1_p3), .in1(registers_1_reg_out_1), .out(multiplexer_7_out), .sel(not_3_out));
  stack stack_1 (
    .clock(controlled_buffer_1_out), .pop(or_5_out), .push(or_4_out), .input_0(multiplexer_9_out),
    .output_0(stack_1_output_0));
  assign controlled_buffer_2_out = or_5_out ? stack_1_output_0 : 16'bz;  // Controlled_Buffer controlled_buffer_5
  or or_3 (or_3_out, decoder_1_out12, decoder_1_out5);
  not not_4 (not_4_out, or_3_out);
  Multiplexer #(.width(16)) multiplexer_8 (
    .in0(rom_1_p4), .in1(registers_1_reg_out_0), .out(multiplexer_8_out), .sel(not_4_out));
  or or_4 (or_4_out, decoder_1_out21, decoder_1_out13);
  not not_5 (not_5_out, decoder_1_out21);
  Multiplexer #(.width(16)) multiplexer_9 (
    .in0(controlled_buffer_3_out), .in1(registers_1_reg_out_1), .out(multiplexer_9_out), .sel(not_5_out));
  or or_5 (or_5_out, decoder_1_out22, decoder_1_out14);
  alu alu_1 (
    .input0(multiplexer_7_out), .input1(multiplexer_8_out), .instruction(rom_1_p2),
    .output1(controlled_buffer_2_out), .jump0(alu_1_jump0));

  // Notes on the sheet:
  //   Instruction Pointer
  //   Instruction Register
  //   Register Load Address 0
  //   Register Load Address 1
  //   Instruction Decoder
  //   128 Kilobytes of Ram
  //   Main System Stack
  //   ALU
endmodule

module alu (
  input  [15:0] instruction,
  input  [15:0] input0,
  input  [15:0] input1,
  output [15:0] output1,
  output jump0
);

  wire adder_2_cout, adder_3_cout, adder_4_cout, and_17_out, and_18_out, decoder_1_out2, decoder_1_out3,
       decoder_1_out4, decoder_1_out5, decoder_1_out6, decoder_1_out7, decoder_1_out8, decoder_1_out9,
       decoder_1_out10, decoder_1_out11, decoder_1_out16, decoder_1_out17, decoder_1_out18, decoder_1_out19,
       decoder_1_out20, decoder_1_out24, equal_to_out, greater_than_out, less_than_out, multiplexer_1_out,
       multiplexer_2_out, multiplexer_3_out, multiplexer_4_out, multiplexer_5_out, not_1_out, not_3_out,
       not_5_out, not_6_out, not_equal_to_out, or_1_out, xnor_1_out, xnor_2_out, xnor_3_out, xnor_4_out,
       xnor_5_out, xnor_6_out, xnor_7_out, xnor_8_out, xnor_9_out, xnor_10_out, xnor_11_out, xnor_12_out,
       xnor_13_out, xnor_14_out, xnor_15_out, xnor_16_out, xnor_17_out, xnor_18_out, xnor_19_out,
       xnor_20_out, xnor_21_out, xnor_22_out, xnor_23_out, xnor_24_out, xnor_25_out, xnor_26_out,
       xnor_27_out, xnor_28_out, xnor_29_out, xnor_30_out, xnor_31_out, xnor_32_out, xnor_33_out,
       xnor_34_out, xnor_35_out, xnor_36_out, xnor_37_out, xnor_38_out, xnor_39_out, xnor_40_out,
       xnor_41_out, xnor_42_out, xnor_43_out, xnor_44_out, xnor_45_out, xnor_46_out, xnor_47_out,
       xnor_48_out, xnor_49_out, xnor_50_out, xnor_51_out, xnor_52_out, xnor_53_out, xnor_54_out,
       xnor_55_out, xnor_56_out, xnor_57_out, xnor_58_out, xnor_59_out, xnor_60_out, xnor_61_out,
       xnor_62_out, xnor_63_out, xnor_64_out;
  wire [4:0] bit_extender_1_out;
  wire [15:0] adder_1_out, adder_2_out, and_16_out, divider_1_out, multiplier_1_out, nor_16_out, not_2_out,
       not_4_out, or_17_out, subtractor_1_out;

  assign output1 = decoder_1_out2 ? input0 : 16'bz;  // Controlled_Buffer controlled_buffer_1
  Bit_Extender #(.in_width(16), .out_width(5)) bit_extender_1 (.in(instruction), .out(bit_extender_1_out));
  Decoder #(.enable("false"), .select(5)) decoder_1 (
    .out2(decoder_1_out2), .out3(decoder_1_out3), .out4(decoder_1_out4), .out5(decoder_1_out5),
    .out6(decoder_1_out6), .out7(decoder_1_out7), .out8(decoder_1_out8), .out9(decoder_1_out9),
    .out10(decoder_1_out10), .out11(decoder_1_out11), .out16(decoder_1_out16), .out17(decoder_1_out17),
    .out18(decoder_1_out18), .out19(decoder_1_out19), .out20(decoder_1_out20), .out24(decoder_1_out24),
    .sel(bit_extender_1_out));  // open: out0, out1, out12, out13, out14, out15, out21, out22, out23, out25, out26, out27, out28, out29, out30, out31
  or or_1 (or_1_out, decoder_1_out3, decoder_1_out4, decoder_1_out5);
  assign output1 = or_1_out ? adder_1_out : 16'bz;  // Controlled_Buffer controlled_buffer_2
  Adder #(.width(16)) adder_1 (.a(input0), .b(input1), .out(adder_1_out));  // open: cin, cout
  assign output1 = decoder_1_out6 ? subtractor_1_out : 16'bz;  // Controlled_Buffer controlled_buffer_3
  Subtractor #(.width(16)) subtractor_1 (.a(input0), .b(input1), .out(subtractor_1_out));  // open: bin, bout
  assign output1 = decoder_1_out7 ? multiplier_1_out : 16'bz;  // Controlled_Buffer controlled_buffer_4
  Multiplier #(.width(16)) multiplier_1 (.a(input0), .b(input1), .out(multiplier_1_out));  // open: cin, cout
  assign output1 = decoder_1_out8 ? divider_1_out : 16'bz;  // Controlled_Buffer controlled_buffer_5
  Divider #(.width(16)) divider_1 (.a(input0), .b(input1), .out(divider_1_out));  // open: upper, rem
  assign output1 = decoder_1_out24 ? adder_2_out : 16'bz;  // Controlled_Buffer controlled_buffer_6
  Adder #(.width(16)) adder_2 (.a(input0), .b(input1), .out(adder_2_out), .cout(adder_2_cout));  // open: cin
  Multiplexer multiplexer_1 (.in0(1'b0), .in1(adder_2_cout), .out(multiplexer_1_out), .sel(decoder_1_out24));
  assign output1 = decoder_1_out9 ? and_16_out : 16'bz;  // Controlled_Buffer controlled_buffer_7
  and and_1 (and_16_out[15], input1[15], input0[15]);
  and and_2 (and_16_out[14], input1[14], input0[14]);
  and and_3 (and_16_out[13], input1[13], input0[13]);
  and and_4 (and_16_out[12], input1[12], input0[12]);
  and and_5 (and_16_out[11], input1[11], input0[11]);
  and and_6 (and_16_out[10], input1[10], input0[10]);
  and and_7 (and_16_out[9], input1[9], input0[9]);
  and and_8 (and_16_out[8], input1[8], input0[8]);
  and and_9 (and_16_out[7], input1[7], input0[7]);
  and and_10 (and_16_out[6], input1[6], input0[6]);
  and and_11 (and_16_out[5], input1[5], input0[5]);
  and and_12 (and_16_out[4], input1[4], input0[4]);
  and and_13 (and_16_out[3], input1[3], input0[3]);
  and and_14 (and_16_out[2], input1[2], input0[2]);
  and and_15 (and_16_out[1], input1[1], input0[1]);
  and and_16 (and_16_out[0], input1[0], input0[0]);
  assign output1 = decoder_1_out10 ? or_17_out : 16'bz;  // Controlled_Buffer controlled_buffer_8
  or or_2 (or_17_out[15], input1[15], input0[15]);
  or or_3 (or_17_out[14], input1[14], input0[14]);
  or or_4 (or_17_out[13], input1[13], input0[13]);
  or or_5 (or_17_out[12], input1[12], input0[12]);
  or or_6 (or_17_out[11], input1[11], input0[11]);
  or or_7 (or_17_out[10], input1[10], input0[10]);
  or or_8 (or_17_out[9], input1[9], input0[9]);
  or or_9 (or_17_out[8], input1[8], input0[8]);
  or or_10 (or_17_out[7], input1[7], input0[7]);
  or or_11 (or_17_out[6], input1[6], input0[6]);
  or or_12 (or_17_out[5], input1[5], input0[5]);
  or or_13 (or_17_out[4], input1[4], input0[4]);
  or or_14 (or_17_out[3], input1[3], input0[3]);
  or or_15 (or_17_out[2], input1[2], input0[2]);
  or or_16 (or_17_out[1], input1[1], input0[1]);
  or or_17 (or_17_out[0], input1[0], input0[0]);
  assign output1 = decoder_1_out11 ? nor_16_out : 16'bz;  // Controlled_Buffer controlled_buffer_9
  nor nor_1 (nor_16_out[15], input1[15], input0[15]);
  nor nor_2 (nor_16_out[14], input1[14], input0[14]);
  nor nor_3 (nor_16_out[13], input1[13], input0[13]);
  nor nor_4 (nor_16_out[12], input1[12], input0[12]);
  nor nor_5 (nor_16_out[11], input1[11], input0[11]);
  nor nor_6 (nor_16_out[10], input1[10], input0[10]);
  nor nor_7 (nor_16_out[9], input1[9], input0[9]);
  nor nor_8 (nor_16_out[8], input1[8], input0[8]);
  nor nor_9 (nor_16_out[7], input1[7], input0[7]);
  nor nor_10 (nor_16_out[6], input1[6], input0[6]);
  nor nor_11 (nor_16_out[5], input1[5], input0[5]);
  nor nor_12 (nor_16_out[4], input1[4], input0[4]);
  nor nor_13 (nor_16_out[3], input1[3], input0[3]);
  nor nor_14 (nor_16_out[2], input1[2], input0[2]);
  nor nor_15 (nor_16_out[1], input1[1], input0[1]);
  nor nor_16 (nor_16_out[0], input1[0], input0[0]);
  xnor xnor_1 (xnor_1_out, input1[15], input0[15]);
  xnor xnor_2 (xnor_2_out, input1[14], input0[14]);
  xnor xnor_3 (xnor_3_out, input1[13], input0[13]);
  xnor xnor_4 (xnor_4_out, input1[12], input0[12]);
  xnor xnor_5 (xnor_5_out, input1[11], input0[11]);
  xnor xnor_6 (xnor_6_out, input1[10], input0[10]);
  xnor xnor_7 (xnor_7_out, input1[9], input0[9]);
  xnor xnor_8 (xnor_8_out, input1[8], input0[8]);
  xnor xnor_9 (xnor_9_out, input1[7], input0[7]);
  xnor xnor_10 (xnor_10_out, input1[6], input0[6]);
  xnor xnor_11 (xnor_11_out, input1[5], input0[5]);
  xnor xnor_12 (xnor_12_out, input1[4], input0[4]);
  xnor xnor_13 (xnor_13_out, input1[3], input0[3]);
  xnor xnor_14 (xnor_14_out, input1[2], input0[2]);
  xnor xnor_15 (xnor_15_out, input1[1], input0[1]);
  xnor xnor_16 (xnor_16_out, input1[0], input0[0]);
  Multiplexer multiplexer_2 (.in0(1'b0), .in1(equal_to_out), .out(multiplexer_2_out), .sel(decoder_1_out17));
  and equal_to (equal_to_out, xnor_1_out, xnor_2_out, xnor_3_out, xnor_4_out, xnor_5_out, xnor_6_out, xnor_7_out, xnor_8_out, xnor_9_out, xnor_10_out, xnor_11_out, xnor_12_out, xnor_13_out, xnor_14_out, xnor_15_out, xnor_16_out);
  xnor xnor_17 (xnor_17_out, input1[15], input0[15]);
  xnor xnor_18 (xnor_18_out, input1[14], input0[14]);
  xnor xnor_19 (xnor_19_out, input1[13], input0[13]);
  xnor xnor_20 (xnor_20_out, input1[12], input0[12]);
  xnor xnor_21 (xnor_21_out, input1[11], input0[11]);
  xnor xnor_22 (xnor_22_out, input1[10], input0[10]);
  xnor xnor_23 (xnor_23_out, input1[9], input0[9]);
  xnor xnor_24 (xnor_24_out, input1[8], input0[8]);
  xnor xnor_25 (xnor_25_out, input1[7], input0[7]);
  xnor xnor_26 (xnor_26_out, input1[6], input0[6]);
  xnor xnor_27 (xnor_27_out, input1[5], input0[5]);
  xnor xnor_28 (xnor_28_out, input1[4], input0[4]);
  xnor xnor_29 (xnor_29_out, input1[3], input0[3]);
  xnor xnor_30 (xnor_30_out, input1[2], input0[2]);
  xnor xnor_31 (xnor_31_out, input1[1], input0[1]);
  xnor xnor_32 (xnor_32_out, input1[0], input0[0]);
  Multiplexer multiplexer_3 (.in0(1'b0), .in1(not_1_out), .out(multiplexer_3_out), .sel(decoder_1_out18));
  not not_1 (not_1_out, not_equal_to_out);
  and not_equal_to (not_equal_to_out, xnor_17_out, xnor_18_out, xnor_19_out, xnor_20_out, xnor_21_out, xnor_22_out, xnor_23_out, xnor_24_out, xnor_25_out, xnor_26_out, xnor_27_out, xnor_28_out, xnor_29_out, xnor_30_out, xnor_31_out, xnor_32_out);
  Adder #(.width(16)) adder_3 (.a(input0), .b(not_2_out), .cout(adder_3_cout));  // open: out, cin
  assign not_2_out = ~input1;  // NOT_Gate not_2, 16 bits wide
  xnor xnor_33 (xnor_33_out, input1[15], input0[15]);
  xnor xnor_34 (xnor_34_out, input1[14], input0[14]);
  xnor xnor_35 (xnor_35_out, input1[13], input0[13]);
  xnor xnor_36 (xnor_36_out, input1[12], input0[12]);
  xnor xnor_37 (xnor_37_out, input1[11], input0[11]);
  xnor xnor_38 (xnor_38_out, input1[10], input0[10]);
  xnor xnor_39 (xnor_39_out, input1[9], input0[9]);
  xnor xnor_40 (xnor_40_out, input1[8], input0[8]);
  xnor xnor_41 (xnor_41_out, input1[7], input0[7]);
  xnor xnor_42 (xnor_42_out, input1[6], input0[6]);
  xnor xnor_43 (xnor_43_out, input1[5], input0[5]);
  xnor xnor_44 (xnor_44_out, input1[4], input0[4]);
  xnor xnor_45 (xnor_45_out, input1[3], input0[3]);
  xnor xnor_46 (xnor_46_out, input1[2], input0[2]);
  xnor xnor_47 (xnor_47_out, input1[1], input0[1]);
  xnor xnor_48 (xnor_48_out, input1[0], input0[0]);
  Multiplexer multiplexer_4 (.in0(1'b0), .in1(and_17_out), .out(multiplexer_4_out), .sel(decoder_1_out19));
  and and_17 (and_17_out, adder_3_cout, not_3_out);
  not not_3 (not_3_out, greater_than_out);
  and greater_than (greater_than_out, xnor_33_out, xnor_34_out, xnor_35_out, xnor_36_out, xnor_37_out, xnor_38_out, xnor_39_out, xnor_40_out, xnor_41_out, xnor_42_out, xnor_43_out, xnor_44_out, xnor_45_out, xnor_46_out, xnor_47_out, xnor_48_out);
  assign not_4_out = ~input1;  // NOT_Gate not_4, 16 bits wide
  Adder #(.width(16)) adder_4 (.a(input0), .b(not_4_out), .cout(adder_4_cout));  // open: out, cin
  not not_5 (not_5_out, adder_4_cout);
  xnor xnor_49 (xnor_49_out, input1[15], input0[15]);
  xnor xnor_50 (xnor_50_out, input1[14], input0[14]);
  xnor xnor_51 (xnor_51_out, input1[13], input0[13]);
  xnor xnor_52 (xnor_52_out, input1[12], input0[12]);
  xnor xnor_53 (xnor_53_out, input1[11], input0[11]);
  xnor xnor_54 (xnor_54_out, input1[10], input0[10]);
  xnor xnor_55 (xnor_55_out, input1[9], input0[9]);
  xnor xnor_56 (xnor_56_out, input1[8], input0[8]);
  xnor xnor_57 (xnor_57_out, input1[7], input0[7]);
  xnor xnor_58 (xnor_58_out, input1[6], input0[6]);
  xnor xnor_59 (xnor_59_out, input1[5], input0[5]);
  xnor xnor_60 (xnor_60_out, input1[4], input0[4]);
  xnor xnor_61 (xnor_61_out, input1[3], input0[3]);
  xnor xnor_62 (xnor_62_out, input1[2], input0[2]);
  xnor xnor_63 (xnor_63_out, input1[1], input0[1]);
  xnor xnor_64 (xnor_64_out, input1[0], input0[0]);
  Multiplexer multiplexer_5 (.in0(1'b0), .in1(and_18_out), .out(multiplexer_5_out), .sel(decoder_1_out20));
  and and_18 (and_18_out, not_5_out, not_6_out);
  or or_18 (jump0, decoder_1_out16, multiplexer_2_out, multiplexer_3_out, multiplexer_4_out, multiplexer_5_out, multiplexer_1_out);
  not not_6 (not_6_out, less_than_out);
  and less_than (less_than_out, xnor_49_out, xnor_50_out, xnor_51_out, xnor_52_out, xnor_53_out, xnor_54_out, xnor_55_out, xnor_56_out, xnor_57_out, xnor_58_out, xnor_59_out, xnor_60_out, xnor_61_out, xnor_62_out, xnor_63_out, xnor_64_out);
endmodule

module stack (
  input  pop,
  input  push,
  input  [15:0] input_0,
  input  clock,
  output [15:0] output_0
);

  wire adder_1_cout, or_1_out;
  wire [15:0] adder_1_out, multiplexer_1_out, multiplexer_2_out, multiplexer_3_out, register_1_q,
       subtractor_1_out;

  Adder #(.width(16)) adder_1 (.a(register_1_q), .b(16'h1), .out(adder_1_out), .cout(adder_1_cout));  // open: cin
  Subtractor #(.width(16)) subtractor_1 (
    .a(register_1_q), .b(16'h1), .out(subtractor_1_out), .bin(adder_1_cout));  // open: bout
  Register #(.width(16)) register_1 (.D(multiplexer_1_out), .en(or_1_out), .clk(clock), .Q(register_1_q));  // open: clr
  Multiplexer #(.width(16)) multiplexer_1 (
    .in0(adder_1_out), .in1(subtractor_1_out), .out(multiplexer_1_out), .sel(pop));
  Multiplexer #(.width(16)) multiplexer_2 (
    .in0(register_1_q), .in1(subtractor_1_out), .out(multiplexer_2_out), .sel(pop));
  RAM #(.addrWidth(16), .asyncread("true"), .dataWidth(16)) ram_1 (
    .addr(multiplexer_2_out), .we(or_1_out), .oe(1'b1), .clk(clock), .din(multiplexer_3_out), .dout(output_0));
  or or_1 (or_1_out, pop, push);
  Multiplexer #(.width(16)) multiplexer_3 (.in0({16{1'b0}}), .in1(input_0), .out(multiplexer_3_out), .sel(push));
endmodule

module registers (
  input  [15:0] reg_save,
  input  [15:0] reg_load_1,
  input  [15:0] reg_load_0,
  input  clock,
  input  [15:0] reg_in,
  output [15:0] reg_out_1,
  output [15:0] reg_out_0
);

  wire decoder_1_out0, decoder_1_out1, decoder_1_out2, decoder_1_out3, decoder_1_out4, decoder_1_out5,
       decoder_1_out6, decoder_1_out7, decoder_1_out8, decoder_1_out9, decoder_1_out10, decoder_1_out11,
       decoder_1_out12, decoder_1_out13, decoder_1_out14, decoder_1_out15, decoder_1_out16, decoder_1_out17,
       decoder_1_out18, decoder_1_out19;
  wire [4:0] bit_extender_1_out, bit_extender_2_out, bit_extender_3_out;
  wire [15:0] reg0_q, reg1_q, reg2_q, reg3_q, reg4_q, reg5_q, reg6_q, reg7_q, reg8_q, reg9_q, reg10_q,
       reg11_q, reg12_q, reg13_q, reg14_q, reg15_q, reg16_q, reg17_q, reg18_q, reg_out_q;

  Bit_Extender #(.in_width(16), .out_width(5)) bit_extender_1 (.in(reg_save), .out(bit_extender_1_out));
  Decoder #(.enable("false"), .select(5)) decoder_1 (
    .out0(decoder_1_out0), .out1(decoder_1_out1), .out2(decoder_1_out2), .out3(decoder_1_out3),
    .out4(decoder_1_out4), .out5(decoder_1_out5), .out6(decoder_1_out6), .out7(decoder_1_out7),
    .out8(decoder_1_out8), .out9(decoder_1_out9), .out10(decoder_1_out10), .out11(decoder_1_out11),
    .out12(decoder_1_out12), .out13(decoder_1_out13), .out14(decoder_1_out14), .out15(decoder_1_out15),
    .out16(decoder_1_out16), .out17(decoder_1_out17), .out18(decoder_1_out18), .out19(decoder_1_out19),
    .sel(bit_extender_1_out));  // open: out20, out21, out22, out23, out24, out25, out26, out27, out28, out29, out30, out31
  Register #(.width(16)) reg0 (.D(reg_in), .en(decoder_1_out0), .clk(clock), .Q(reg0_q));  // open: clr
  Register #(.width(16)) reg1 (.D(reg_in), .en(decoder_1_out1), .clk(clock), .Q(reg1_q));  // open: clr
  Register #(.width(16)) reg2 (.D(reg_in), .en(decoder_1_out2), .clk(clock), .Q(reg2_q));  // open: clr
  Register #(.width(16)) reg3 (.D(reg_in), .en(decoder_1_out3), .clk(clock), .Q(reg3_q));  // open: clr
  Register #(.width(16)) reg4 (.D(reg_in), .en(decoder_1_out4), .clk(clock), .Q(reg4_q));  // open: clr
  Register #(.width(16)) reg5 (.D(reg_in), .en(decoder_1_out5), .clk(clock), .Q(reg5_q));  // open: clr
  Register #(.width(16)) reg6 (.D(reg_in), .en(decoder_1_out6), .clk(clock), .Q(reg6_q));  // open: clr
  Register #(.width(16)) reg7 (.D(reg_in), .en(decoder_1_out7), .clk(clock), .Q(reg7_q));  // open: clr
  Register #(.width(16)) reg8 (.D(reg_in), .en(decoder_1_out8), .clk(clock), .Q(reg8_q));  // open: clr
  Register #(.width(16)) reg9 (.D(reg_in), .en(decoder_1_out9), .clk(clock), .Q(reg9_q));  // open: clr
  Register #(.width(16)) reg10 (.D(reg_in), .en(decoder_1_out10), .clk(clock), .Q(reg10_q));  // open: clr
  Register #(.width(16)) reg11 (.D(reg_in), .en(decoder_1_out11), .clk(clock), .Q(reg11_q));  // open: clr
  Register #(.width(16)) reg12 (.D(reg_in), .en(decoder_1_out12), .clk(clock), .Q(reg12_q));  // open: clr
  Register #(.width(16)) reg13 (.D(reg_in), .en(decoder_1_out13), .clk(clock), .Q(reg13_q));  // open: clr
  Register #(.width(16)) reg14 (.D(reg_in), .en(decoder_1_out14), .clk(clock), .Q(reg14_q));  // open: clr
  Register #(.width(16)) reg15 (.D(reg_in), .en(decoder_1_out15), .clk(clock), .Q(reg15_q));  // open: clr
  Register #(.width(16)) reg16 (.D(reg_in), .en(decoder_1_out16), .clk(clock), .Q(reg16_q));  // open: clr
  Register #(.width(16)) reg17 (.D(reg_in), .en(decoder_1_out17), .clk(clock), .Q(reg17_q));  // open: clr
  Register #(.width(16)) reg18 (.D(reg_in), .en(decoder_1_out18), .clk(clock), .Q(reg18_q));  // open: clr
  Register #(.width(16)) reg_out (.D(reg_in), .en(decoder_1_out19), .clk(clock), .Q(reg_out_q));  // open: clr
  Bit_Extender #(.in_width(16), .out_width(5)) bit_extender_2 (.in(reg_load_1), .out(bit_extender_2_out));
  Multiplexer #(.select(5), .width(16)) multiplexer_1 (
    .in0(reg0_q), .in1(reg1_q), .in2(reg2_q), .in3(reg3_q), .in4(reg4_q), .in5(reg5_q), .in6(reg6_q),
    .in7(reg7_q), .in8(reg8_q), .in9(reg9_q), .in10(reg10_q), .in11(reg11_q), .in12(reg12_q), .in13(reg13_q),
    .in14(reg14_q), .in15(reg15_q), .in16(reg16_q), .in17(reg17_q), .in18(reg18_q), .in19(reg_out_q),
    .out(reg_out_1), .sel(bit_extender_2_out));  // open: in20, in21, in22, in23, in24, in25, in26, in27, in28, in29, in30, in31
  Bit_Extender #(.in_width(16), .out_width(5)) bit_extender_3 (.in(reg_load_0), .out(bit_extender_3_out));
  Multiplexer #(.select(5), .width(16)) multiplexer_2 (
    .in0(reg0_q), .in1(reg1_q), .in2(reg2_q), .in3(reg3_q), .in4(reg4_q), .in5(reg5_q), .in6(reg6_q),
    .in7(reg7_q), .in8(reg8_q), .in9(reg9_q), .in10(reg10_q), .in11(reg11_q), .in12(reg12_q), .in13(reg13_q),
    .in14(reg14_q), .in15(reg15_q), .in16(reg16_q), .in17(reg17_q), .in18(reg18_q), .in19(reg_out_q),
    .out(reg_out_0), .sel(bit_extender_3_out));  // open: in20, in21, in22, in23, in24, in25, in26, in27, in28, in29, in30, in31
endmodule
